# Fritzing sketch Quad_Creek (saved by Fritzing 1.0.4)
circuit board: 27.5cm x 14cm
breadboards: 1

parts:
  R4 = Rotary Potentiometer (Small) [maximum_resistance=10kΩ knob_status=50% power=0.5W package=THT]
  R5 = Rotary Potentiometer (Small) [maximum_resistance=10kΩ knob_status=50% power=0.5W package=THT]
  R7 = Rotary Potentiometer (Small) [maximum_resistance=10kΩ knob_status=50% power=0.5W package=THT]
  R8 = Rotary Potentiometer (Small) [maximum_resistance=10kΩ knob_status=50% power=0.5W package=THT]
  R9 = Rotary Potentiometer (Small) [maximum_resistance=10kΩ knob_status=50% power=0.5W package=THT]
  R10 = Rotary Potentiometer (Small) [maximum_resistance=10kΩ knob_status=50% power=0.5W package=THT]
  R11 = Rotary Potentiometer (Small) [maximum_resistance=10kΩ knob_status=50% power=0.5W package=THT]
  R12 = Rotary Potentiometer (Small) [maximum_resistance=10kΩ knob_status=50% power=0.5W package=THT]
  R13 = Rotary Potentiometer (Small) [maximum_resistance=10kΩ knob_status=50% power=0.5W package=THT]
  R16 = Rotary Potentiometer (Small) [maximum_resistance=10kΩ knob_status=50% power=0.5W package=THT]
  R17 = Rotary Potentiometer (Small) [maximum_resistance=10kΩ knob_status=50% power=0.5W package=THT]
  R18 = Rotary Potentiometer (Small) [maximum_resistance=10kΩ knob_status=50% power=0.5W package=THT]
  R19 = Rotary Potentiometer (Small) [maximum_resistance=10kΩ knob_status=50% power=0.5W package=THT]
  R20 = Rotary Potentiometer (Small) [maximum_resistance=10kΩ knob_status=50% power=0.5W package=THT]
  R21 = Rotary Potentiometer (Small) [maximum_resistance=10kΩ knob_status=50% power=0.5W package=THT]
  R22 = Rotary Potentiometer (Small) [maximum_resistance=10kΩ knob_status=50% power=0.5W package=THT]
  100k = Resistor [tolerance=±5% power=0.25W resistance=220 package=THT]
  100k_2 = Resistor [tolerance=±5% power=0.25W resistance=220 package=THT]
  100k_3 = Resistor [tolerance=±5% power=0.25W resistance=220 package=THT]
  100k_4 = Resistor [tolerance=±5% power=0.25W resistance=220 package=THT]
  - = Resistor [tolerance=±5% power=0.25W resistance=220 package=THT]
  -_2 = Resistor [tolerance=±5% power=0.25W resistance=220 package=THT]
  -_3 = Resistor [tolerance=±5% power=0.25W resistance=220 package=THT]
  -_4 = Resistor [tolerance=±5% power=0.25W resistance=220 package=THT]
  -_5 = Resistor [tolerance=±5% power=0.25W resistance=220 package=THT]
  -_6 = Resistor [tolerance=±5% power=0.25W resistance=220 package=THT]
  -_7 = Resistor [tolerance=±5% power=0.25W resistance=220 package=THT]
  -_8 = Resistor [tolerance=±5% power=0.25W resistance=220 package=THT]
  1k = Resistor [tolerance=±5% power=0.25W resistance=220 package=THT]
  1k_2 = Resistor [tolerance=±5% power=0.25W resistance=220 package=THT]
  TL082 = IC, DIP package, 8 pins [chip_label=IC]
  100k_5 = Resistor [tolerance=±5% power=0.25W resistance=220 package=THT]
  100k_6 = Resistor [tolerance=±5% power=0.25W resistance=220 package=THT]
  100k_7 = Resistor [tolerance=±5% power=0.25W resistance=220 package=THT]
  100k_8 = Resistor [tolerance=±5% power=0.25W resistance=220 package=THT]
  105 = Ceramic Capacitor [capacitance=100nF voltage=35V package="200 mil [THT, multilayer]"]
  105_2 = Ceramic Capacitor [capacitance=100nF voltage=35V package="200 mil [THT, multilayer]"]
  1k_3 = Resistor [tolerance=±5% power=0.25W resistance=220 package=THT]
  1k_4 = Resistor [tolerance=±5% power=0.25W resistance=220 package=THT]
  105_3 = Ceramic Capacitor [capacitance=100nF voltage=35V package="200 mil [THT, multilayer]"]
  105_4 = Ceramic Capacitor [capacitance=100nF voltage=35V package="200 mil [THT, multilayer]"]
  104 = Ceramic Capacitor [capacitance=100nF voltage=35V package="200 mil [THT, multilayer]"]
  ʃ = Resistor [tolerance=±5% power=0.25W resistance=220 package=THT]
  ʃ_2 = Resistor [tolerance=±5% power=0.25W resistance=220 package=THT]
  100k_9 = Resistor [tolerance=±5% power=0.25W resistance=220 package=THT]
  102 = Ceramic Capacitor [capacitance=100nF voltage=35V package="200 mil [THT, multilayer]"]
  ʃ_3 = Resistor [tolerance=±5% power=0.25W resistance=220 package=THT]
  ʃ_4 = Resistor [tolerance=±5% power=0.25W resistance=220 package=THT]
  102_2 = Ceramic Capacitor [capacitance=100nF voltage=35V package="200 mil [THT, multilayer]"]
  100k_10 = Resistor [tolerance=±5% power=0.25W resistance=220 package=THT]
  ▯ = Arduino Nano (Rev3.0)
  TL082_2 = IC, DIP package, 8 pins [chip_label=IC]
  ʃ_5 = Resistor [tolerance=±5% power=0.25W resistance=220 package=THT]
  ʃ_6 = Resistor [tolerance=±5% power=0.25W resistance=220 package=THT]
  1k_5 = Resistor [tolerance=±5% power=0.25W resistance=220 package=THT]
  102_3 = Ceramic Capacitor [capacitance=100nF voltage=35V package="200 mil [THT, multilayer]"]
  10k = Resistor [tolerance=±5% power=0.25W resistance=220 package=THT]
  2_2k = Resistor [tolerance=±5% power=0.25W resistance=220 package=THT]
  2_2k_2 = Resistor [tolerance=±5% power=0.25W resistance=220 package=THT]
  1k_6 = Resistor [tolerance=±5% power=0.25W resistance=220 package=THT]
  102_4 = Ceramic Capacitor [capacitance=100nF voltage=35V package="200 mil [THT, multilayer]"]
  100k_11 = Resistor [tolerance=±5% power=0.25W resistance=220 package=THT]
  102_5 = Ceramic Capacitor [capacitance=100nF voltage=35V package="200 mil [THT, multilayer]"]
  100k_12 = Resistor [tolerance=±5% power=0.25W resistance=220 package=THT]
  ʃ_7 = Resistor [tolerance=±5% power=0.25W resistance=220 package=THT]
  ʃ_8 = Resistor [tolerance=±5% power=0.25W resistance=220 package=THT]
  ʃ_9 = Resistor [tolerance=±5% power=0.25W resistance=220 package=THT]
  100k_13 = Resistor [tolerance=±5% power=0.25W resistance=220 package=THT]
  1k_7 = Resistor [tolerance=±5% power=0.25W resistance=220 package=THT]
  102_6 = Ceramic Capacitor [capacitance=100nF voltage=35V package="200 mil [THT, multilayer]"]
  1k_8 = Resistor [tolerance=±5% power=0.25W resistance=220 package=THT]
  ʃ_10 = Resistor [tolerance=±5% power=0.25W resistance=220 package=THT]
  ʃ_11 = Resistor [tolerance=±5% power=0.25W resistance=220 package=THT]
  100k_14 = Resistor [tolerance=±5% power=0.25W resistance=220 package=THT]
  102_7 = Ceramic Capacitor [capacitance=100nF voltage=35V package="200 mil [THT, multilayer]"]
  100k1 = Resistor [tolerance=±5% power=0.25W resistance=220 package=THT]
  100k2 = Resistor [tolerance=±5% power=0.25W resistance=220 package=THT]
  100k3 = Resistor [tolerance=±5% power=0.25W resistance=220 package=THT]
  100k4 = Resistor [tolerance=±5% power=0.25W resistance=220 package=THT]
  100k5 = Resistor [tolerance=±5% power=0.25W resistance=220 package=THT]
  1k_9 = Resistor [tolerance=±5% power=0.25W resistance=220 package=THT]
  100k_15 = Resistor [tolerance=±5% power=0.25W resistance=220 package=THT]
  ʃ_12 = Resistor [tolerance=±5% power=0.25W resistance=220 package=THT]
  ʃ_13 = Resistor [tolerance=±5% power=0.25W resistance=220 package=THT]
  ʃ_14 = Resistor [tolerance=±5% power=0.25W resistance=220 package=THT]
  1k_10 = Resistor [tolerance=±5% power=0.25W resistance=220 package=THT]
  ʃ_15 = Resistor [tolerance=±5% power=0.25W resistance=220 package=THT]
  ʃ_16 = Resistor [tolerance=±5% power=0.25W resistance=220 package=THT]
  100k_16 = Resistor [tolerance=±5% power=0.25W resistance=220 package=THT]
  102_8 = Ceramic Capacitor [capacitance=100nF voltage=35V package="200 mil [THT, multilayer]"]
  105_5 = Ceramic Capacitor [capacitance=100nF voltage=35V package="200 mil [THT, multilayer]"]
  22k = Resistor [tolerance=±5% power=0.25W resistance=220 package=THT]
  22k_2 = Resistor [tolerance=±5% power=0.25W resistance=220 package=THT]
  103 = Ceramic Capacitor [capacitance=100nF voltage=35V package="200 mil [THT, multilayer]"]
  103_2 = Ceramic Capacitor [capacitance=100nF voltage=35V package="200 mil [THT, multilayer]"]
  22k_3 = Resistor [tolerance=±5% power=0.25W resistance=220 package=THT]
  -_9 = NPN-Transistor [package="TO92 [THT]"]
  1M = Resistor [tolerance=±5% power=0.25W resistance=220 package=THT]
  102_9 = Ceramic Capacitor [capacitance=100nF voltage=35V package="200 mil [THT, multilayer]"]
  -_10 = Resistor [tolerance=±5% power=0.25W resistance=220 package=THT]
  22k_4 = Resistor [tolerance=±5% power=0.25W resistance=220 package=THT]
  102_10 = Ceramic Capacitor [capacitance=100nF voltage=35V package="200 mil [THT, multilayer]"]
  10k_2 = Resistor [tolerance=±5% power=0.25W resistance=220 package=THT]
  10k_3 = Resistor [tolerance=±5% power=0.25W resistance=220 package=THT]
  LM358 = IC, DIP package, 8 pins [chip_label=IC]
  101 = Ceramic Capacitor [capacitance=100nF voltage=35V package="200 mil [THT, multilayer]"]
  47k = Resistor [tolerance=±5% power=0.25W resistance=220 package=THT]
  1M_2 = Resistor [tolerance=±5% power=0.25W resistance=220 package=THT]
  105_6 = Ceramic Capacitor [capacitance=100nF voltage=35V package="200 mil [THT, multilayer]"]
  4_7k = Resistor [tolerance=±5% power=0.25W resistance=220 package=THT]
  2_2M = Resistor [tolerance=±5% power=0.25W resistance=220 package=THT]
  102_11 = Ceramic Capacitor [capacitance=100nF voltage=35V package="200 mil [THT, multilayer]"]
  -_11 = NPN-Transistor [package="TO92 [THT]"]
  104_2 = Ceramic Capacitor [capacitance=100nF voltage=35V package="200 mil [THT, multilayer]"]
  N = NPN-Transistor [package="TO92 [THT]"]
  220k = Resistor [tolerance=±5% power=0.25W resistance=220 package=THT]
  47k_2 = Resistor [tolerance=±5% power=0.25W resistance=220 package=THT]
  10k_4 = Resistor [tolerance=±5% power=0.25W resistance=220 package=THT]
  102_12 = Ceramic Capacitor [capacitance=100nF voltage=35V package="200 mil [THT, multilayer]"]
  10k_5 = Resistor [tolerance=±5% power=0.25W resistance=220 package=THT]
  104_3 = Ceramic Capacitor [capacitance=100nF voltage=35V package="200 mil [THT, multilayer]"]
  L7809CV = Voltage Regulator [package=to220-igo]
  D1 = Rectifier Diode [part_number=1N4001 package="300 mil [THT]"]
  220uF = Electrolytic Capacitor [capacitance=1µF voltage=35V package="100 mil [THT, electrolytic]"]
  10uF = Electrolytic Capacitor [capacitance=1µF voltage=35V package="100 mil [THT, electrolytic]"]
  10k_6 = Resistor [tolerance=±5% power=0.25W resistance=220 package=THT]
  10k_7 = Resistor [tolerance=±5% power=0.25W resistance=220 package=THT]
  104_4 = Ceramic Capacitor [capacitance=100nF voltage=35V package="200 mil [THT, multilayer]"]
  106 = Ceramic Capacitor [capacitance=100nF voltage=35V package="200 mil [THT, multilayer]"]
  475 = Ceramic Capacitor [capacitance=100nF voltage=35V package="200 mil [THT, multilayer]"]
  104_5 = Ceramic Capacitor [capacitance=100nF voltage=35V package="200 mil [THT, multilayer]"]
  104_6 = Ceramic Capacitor [capacitance=100nF voltage=35V package="200 mil [THT, multilayer]"]
  106_2 = Ceramic Capacitor [capacitance=100nF voltage=35V package="200 mil [THT, multilayer]"]
  106_3 = Ceramic Capacitor [capacitance=100nF voltage=35V package="200 mil [THT, multilayer]"]
  104_7 = Ceramic Capacitor [capacitance=100nF voltage=35V package="200 mil [THT, multilayer]"]
  104_8 = Ceramic Capacitor [capacitance=100nF voltage=35V package="200 mil [THT, multilayer]"]
  105_7 = Ceramic Capacitor [capacitance=100nF voltage=35V package="200 mil [THT, multilayer]"]
  104_9 = Ceramic Capacitor [capacitance=100nF voltage=35V package="200 mil [THT, multilayer]"]
  105_8 = Ceramic Capacitor [capacitance=100nF voltage=35V package="200 mil [THT, multilayer]"]
  1k_11 = Resistor [tolerance=±5% power=0.25W resistance=220 package=THT]
  1k_12 = Resistor [tolerance=±5% power=0.25W resistance=220 package=THT]
  10k_8 = Resistor [tolerance=±5% power=0.25W resistance=220 package=THT]
  10k_9 = Resistor [tolerance=±5% power=0.25W resistance=220 package=THT]
  105_9 = Ceramic Capacitor [capacitance=100nF voltage=35V package="200 mil [THT, multilayer]"]
  1k_13 = Resistor [tolerance=±5% power=0.25W resistance=220 package=THT]
  1k_14 = Resistor [tolerance=±5% power=0.25W resistance=220 package=THT]
  CD4013 = IC, DIP package, 14 pins [chip_label=CD4013]
  220k1 = Resistor [tolerance=±5% power=0.25W resistance=220 package=THT]
  220k_2 = Resistor [tolerance=±5% power=0.25W resistance=220 package=THT]
  103_3 = Ceramic Capacitor [capacitance=100nF voltage=35V package="200 mil [THT, multilayer]"]
  103_4 = Ceramic Capacitor [capacitance=100nF voltage=35V package="200 mil [THT, multilayer]"]
  103_5 = Ceramic Capacitor [capacitance=100nF voltage=35V package="200 mil [THT, multilayer]"]
  105_10 = Ceramic Capacitor [capacitance=100nF voltage=35V package="200 mil [THT, multilayer]"]
  105_11 = Ceramic Capacitor [capacitance=100nF voltage=35V package="200 mil [THT, multilayer]"]
  103_6 = Ceramic Capacitor [capacitance=100nF voltage=35V package="200 mil [THT, multilayer]"]
  -_12 = NPN-Transistor [package="TO92 [THT]"]
  -_13 = NPN-Transistor [package="TO92 [THT]"]
  -_14 = NPN-Transistor [package="TO92 [THT]"]
  -_15 = NPN-Transistor [package="TO92 [THT]"]
  TL082_3 = IC, DIP package, 8 pins [chip_label=IC]
  LM358_2 = IC, DIP package, 8 pins [chip_label=IC]
  LM358_3 = IC, DIP package, 8 pins [chip_label=IC]
  LM358_4 = IC, DIP package, 8 pins [chip_label=IC]
  TL082_4 = IC, DIP package, 8 pins [chip_label=IC]
  -_16 = Resistor [tolerance=±5% power=0.25W resistance=220 package=THT]
  -_17 = Resistor [tolerance=±5% power=0.25W resistance=220 package=THT]
  -_18 = Resistor [tolerance=±5% power=0.25W resistance=220 package=THT]
  -_19 = Resistor [tolerance=±5% power=0.25W resistance=220 package=THT]
  -_20 = Resistor [tolerance=±5% power=0.25W resistance=220 package=THT]
  100k_17 = Resistor [tolerance=±5% power=0.25W resistance=220 package=THT]
  100k_18 = Resistor [tolerance=±5% power=0.25W resistance=220 package=THT]
  100k_19 = Resistor [tolerance=±5% power=0.25W resistance=220 package=THT]
  100k_20 = Resistor [tolerance=±5% power=0.25W resistance=220 package=THT]
  100k_21 = Resistor [tolerance=±5% power=0.25W resistance=220 package=THT]
  100k_22 = Resistor [tolerance=±5% power=0.25W resistance=220 package=THT]
  100k_23 = Resistor [tolerance=±5% power=0.25W resistance=220 package=THT]
  22k_5 = Resistor [tolerance=±5% power=0.25W resistance=220 package=THT]
  22k_6 = Resistor [tolerance=±5% power=0.25W resistance=220 package=THT]
  220k_3 = Resistor [tolerance=±5% power=0.25W resistance=220 package=THT]
  220k_4 = Resistor [tolerance=±5% power=0.25W resistance=220 package=THT]
  220k_5 = Resistor [tolerance=±5% power=0.25W resistance=220 package=THT]
  220k_6 = Resistor [tolerance=±5% power=0.25W resistance=220 package=THT]
  220k_7 = Resistor [tolerance=±5% power=0.25W resistance=220 package=THT]
  1M_3 = Resistor [tolerance=±5% power=0.25W resistance=220 package=THT]
  47k_3 = Resistor [tolerance=±5% power=0.25W resistance=220 package=THT]
  220k_8 = Resistor [tolerance=±5% power=0.25W resistance=220 package=THT]
  1M_4 = Resistor [tolerance=±5% power=0.25W resistance=220 package=THT]
  47k_4 = Resistor [tolerance=±5% power=0.25W resistance=220 package=THT]
  10k_10 = Resistor [tolerance=±5% power=0.25W resistance=220 package=THT]
  10k_11 = Resistor [tolerance=±5% power=0.25W resistance=220 package=THT]
  22k_7 = Resistor [tolerance=±5% power=0.25W resistance=220 package=THT]
  22k_8 = Resistor [tolerance=±5% power=0.25W resistance=220 package=THT]
  10k_12 = Resistor [tolerance=±5% power=0.25W resistance=220 package=THT]
  10k_13 = Resistor [tolerance=±5% power=0.25W resistance=220 package=THT]
  10k_14 = Resistor [tolerance=±5% power=0.25W resistance=220 package=THT]
  10k_15 = Resistor [tolerance=±5% power=0.25W resistance=220 package=THT]
  10k_16 = Resistor [tolerance=±5% power=0.25W resistance=220 package=THT]
  10k_17 = Resistor [tolerance=±5% power=0.25W resistance=220 package=THT]
  100k_24 = Resistor [tolerance=±5% power=0.25W resistance=220 package=THT]
  100k_25 = Resistor [tolerance=±5% power=0.25W resistance=220 package=THT]
  100k_26 = Resistor [tolerance=±5% power=0.25W resistance=220 package=THT]
  100k_27 = Resistor [tolerance=±5% power=0.25W resistance=220 package=THT]
  10k_18 = Resistor [tolerance=±5% power=0.25W resistance=220 package=THT]
  10k_19 = Resistor [tolerance=±5% power=0.25W resistance=220 package=THT]
  -_21 = Resistor [tolerance=±5% power=0.25W resistance=220 package=THT]
  10k_20 = Resistor [tolerance=±5% power=0.25W resistance=220 package=THT]
  10k_21 = Resistor [tolerance=±5% power=0.25W resistance=220 package=THT]
  -_22 = Resistor [tolerance=±5% power=0.25W resistance=220 package=THT]
  100k_28 = Resistor [tolerance=±5% power=0.25W resistance=220 package=THT]
  100k_29 = Resistor [tolerance=±5% power=0.25W resistance=220 package=THT]
  100k19 = Resistor [tolerance=±5% power=0.25W resistance=220 package=THT]
  -_23 = Resistor [tolerance=±5% power=0.25W resistance=220 package=THT]
  100k_30 = Resistor [tolerance=±5% power=0.25W resistance=220 package=THT]
  100k_31 = Resistor [tolerance=±5% power=0.25W resistance=220 package=THT]
  100k_32 = Resistor [tolerance=±5% power=0.25W resistance=220 package=THT]
  100k_33 = Resistor [tolerance=±5% power=0.25W resistance=220 package=THT]
  100k_34 = Resistor [tolerance=±5% power=0.25W resistance=220 package=THT]
  100k_35 = Resistor [tolerance=±5% power=0.25W resistance=220 package=THT]
  104_10 = Ceramic Capacitor [capacitance=100nF voltage=35V package="200 mil [THT, multilayer]"]
  104_11 = Ceramic Capacitor [capacitance=100nF voltage=35V package="200 mil [THT, multilayer]"]
  104_12 = Ceramic Capacitor [capacitance=100nF voltage=35V package="200 mil [THT, multilayer]"]
  104_13 = Ceramic Capacitor [capacitance=100nF voltage=35V package="200 mil [THT, multilayer]"]
  104_14 = Ceramic Capacitor [capacitance=100nF voltage=35V package="200 mil [THT, multilayer]"]
  104_15 = Ceramic Capacitor [capacitance=100nF voltage=35V package="200 mil [THT, multilayer]"]
  104_16 = Ceramic Capacitor [capacitance=100nF voltage=35V package="200 mil [THT, multilayer]"]
  R23 = Rotary Potentiometer (Small) [maximum_resistance=10kΩ knob_status=50% power=0.5W package=THT]
  R24 = Rotary Potentiometer (Small) [maximum_resistance=10kΩ knob_status=50% power=0.5W package=THT]
  R25 = Rotary Potentiometer (Small) [maximum_resistance=10kΩ knob_status=50% power=0.5W package=THT]
  R26 = Rotary Potentiometer (Small) [maximum_resistance=10kΩ knob_status=50% power=0.5W package=THT]
  R27 = Rotary Potentiometer (Small) [maximum_resistance=10kΩ knob_status=50% power=0.5W package=THT]
  R28 = Rotary Potentiometer (Small) [maximum_resistance=10kΩ knob_status=50% power=0.5W package=THT]
  R29 = Rotary Potentiometer (Small) [maximum_resistance=10kΩ knob_status=50% power=0.5W package=THT]
  R30 = Rotary Potentiometer (Small) [maximum_resistance=10kΩ knob_status=50% power=0.5W package=THT]
  106_4 = Ceramic Capacitor [capacitance=100nF voltage=35V package="200 mil [THT, multilayer]"]
  475_2 = Ceramic Capacitor [capacitance=100nF voltage=35V package="200 mil [THT, multilayer]"]
  104_17 = Ceramic Capacitor [capacitance=100nF voltage=35V package="200 mil [THT, multilayer]"]
  104_18 = Ceramic Capacitor [capacitance=100nF voltage=35V package="200 mil [THT, multilayer]"]
  106_5 = Ceramic Capacitor [capacitance=100nF voltage=35V package="200 mil [THT, multilayer]"]
  106_6 = Ceramic Capacitor [capacitance=100nF voltage=35V package="200 mil [THT, multilayer]"]
  104_19 = Ceramic Capacitor [capacitance=100nF voltage=35V package="200 mil [THT, multilayer]"]
  104_20 = Ceramic Capacitor [capacitance=100nF voltage=35V package="200 mil [THT, multilayer]"]
  105_12 = Ceramic Capacitor [capacitance=100nF voltage=35V package="200 mil [THT, multilayer]"]
  104_21 = Ceramic Capacitor [capacitance=100nF voltage=35V package="200 mil [THT, multilayer]"]
  105_13 = Ceramic Capacitor [capacitance=100nF voltage=35V package="200 mil [THT, multilayer]"]
  1k_15 = Resistor [tolerance=±5% power=0.25W resistance=220 package=THT]
  1k_16 = Resistor [tolerance=±5% power=0.25W resistance=220 package=THT]
  10k_22 = Resistor [tolerance=±5% power=0.25W resistance=220 package=THT]
  10k_23 = Resistor [tolerance=±5% power=0.25W resistance=220 package=THT]
  105_14 = Ceramic Capacitor [capacitance=100nF voltage=35V package="200 mil [THT, multilayer]"]
  1k_17 = Resistor [tolerance=±5% power=0.25W resistance=220 package=THT]
  1k_18 = Resistor [tolerance=±5% power=0.25W resistance=220 package=THT]
  CD4013_2 = IC, DIP package, 14 pins [chip_label=CD4013]
  220k_9 = Resistor [tolerance=±5% power=0.25W resistance=220 package=THT]
  220k_10 = Resistor [tolerance=±5% power=0.25W resistance=220 package=THT]
  103_7 = Ceramic Capacitor [capacitance=100nF voltage=35V package="200 mil [THT, multilayer]"]
  103_8 = Ceramic Capacitor [capacitance=100nF voltage=35V package="200 mil [THT, multilayer]"]
  103_9 = Ceramic Capacitor [capacitance=100nF voltage=35V package="200 mil [THT, multilayer]"]
  105_15 = Ceramic Capacitor [capacitance=100nF voltage=35V package="200 mil [THT, multilayer]"]
  105_16 = Ceramic Capacitor [capacitance=100nF voltage=35V package="200 mil [THT, multilayer]"]
  103_10 = Ceramic Capacitor [capacitance=100nF voltage=35V package="200 mil [THT, multilayer]"]
  -_24 = NPN-Transistor [package="TO92 [THT]"]
  -_25 = NPN-Transistor [package="TO92 [THT]"]
  -_26 = NPN-Transistor [package="TO92 [THT]"]
  -_27 = NPN-Transistor [package="TO92 [THT]"]
  TL082_5 = IC, DIP package, 8 pins [chip_label=IC]
  LM358_5 = IC, DIP package, 8 pins [chip_label=IC]
  LM358_6 = IC, DIP package, 8 pins [chip_label=IC]
  LM358_7 = IC, DIP package, 8 pins [chip_label=IC]
  TL082_6 = IC, DIP package, 8 pins [chip_label=IC]
  -_28 = Resistor [tolerance=±5% power=0.25W resistance=220 package=THT]
  -_29 = Resistor [tolerance=±5% power=0.25W resistance=220 package=THT]
  -_30 = Resistor [tolerance=±5% power=0.25W resistance=220 package=THT]
  -_31 = Resistor [tolerance=±5% power=0.25W resistance=220 package=THT]
  -_32 = Resistor [tolerance=±5% power=0.25W resistance=220 package=THT]
  100k_36 = Resistor [tolerance=±5% power=0.25W resistance=220 package=THT]
  100k_37 = Resistor [tolerance=±5% power=0.25W resistance=220 package=THT]
  100k_38 = Resistor [tolerance=±5% power=0.25W resistance=220 package=THT]
  100k_39 = Resistor [tolerance=±5% power=0.25W resistance=220 package=THT]
  100k_40 = Resistor [tolerance=±5% power=0.25W resistance=220 package=THT]
  100k_41 = Resistor [tolerance=±5% power=0.25W resistance=220 package=THT]
  100k_42 = Resistor [tolerance=±5% power=0.25W resistance=220 package=THT]
  22k_9 = Resistor [tolerance=±5% power=0.25W resistance=220 package=THT]
  22k_10 = Resistor [tolerance=±5% power=0.25W resistance=220 package=THT]
  220k_11 = Resistor [tolerance=±5% power=0.25W resistance=220 package=THT]
  220k_12 = Resistor [tolerance=±5% power=0.25W resistance=220 package=THT]
  220k_13 = Resistor [tolerance=±5% power=0.25W resistance=220 package=THT]
  220k_14 = Resistor [tolerance=±5% power=0.25W resistance=220 package=THT]
  220k_15 = Resistor [tolerance=±5% power=0.25W resistance=220 package=THT]
  1M_5 = Resistor [tolerance=±5% power=0.25W resistance=220 package=THT]
  47k_5 = Resistor [tolerance=±5% power=0.25W resistance=220 package=THT]
  220k_16 = Resistor [tolerance=±5% power=0.25W resistance=220 package=THT]
  1M_6 = Resistor [tolerance=±5% power=0.25W resistance=220 package=THT]
  47k_6 = Resistor [tolerance=±5% power=0.25W resistance=220 package=THT]
  10k_24 = Resistor [tolerance=±5% power=0.25W resistance=220 package=THT]
  10k_25 = Resistor [tolerance=±5% power=0.25W resistance=220 package=THT]
  22k_11 = Resistor [tolerance=±5% power=0.25W resistance=220 package=THT]
  22k_12 = Resistor [tolerance=±5% power=0.25W resistance=220 package=THT]
  10k_26 = Resistor [tolerance=±5% power=0.25W resistance=220 package=THT]
  10k_27 = Resistor [tolerance=±5% power=0.25W resistance=220 package=THT]
  10k_28 = Resistor [tolerance=±5% power=0.25W resistance=220 package=THT]
  10k_29 = Resistor [tolerance=±5% power=0.25W resistance=220 package=THT]
  10k_30 = Resistor [tolerance=±5% power=0.25W resistance=220 package=THT]
  10k_31 = Resistor [tolerance=±5% power=0.25W resistance=220 package=THT]
  100k_43 = Resistor [tolerance=±5% power=0.25W resistance=220 package=THT]
  100k_44 = Resistor [tolerance=±5% power=0.25W resistance=220 package=THT]
  100k_45 = Resistor [tolerance=±5% power=0.25W resistance=220 package=THT]
  100k_46 = Resistor [tolerance=±5% power=0.25W resistance=220 package=THT]
  10k_32 = Resistor [tolerance=±5% power=0.25W resistance=220 package=THT]
  10k_33 = Resistor [tolerance=±5% power=0.25W resistance=220 package=THT]
  -_33 = Resistor [tolerance=±5% power=0.25W resistance=220 package=THT]
  10k_34 = Resistor [tolerance=±5% power=0.25W resistance=220 package=THT]
  10k_35 = Resistor [tolerance=±5% power=0.25W resistance=220 package=THT]
  -_34 = Resistor [tolerance=±5% power=0.25W resistance=220 package=THT]
  100k_47 = Resistor [tolerance=±5% power=0.25W resistance=220 package=THT]
  100k_48 = Resistor [tolerance=±5% power=0.25W resistance=220 package=THT]
  100k_49 = Resistor [tolerance=±5% power=0.25W resistance=220 package=THT]
  -_35 = Resistor [tolerance=±5% power=0.25W resistance=220 package=THT]
  100k_50 = Resistor [tolerance=±5% power=0.25W resistance=220 package=THT]
  100k_51 = Resistor [tolerance=±5% power=0.25W resistance=220 package=THT]
  100k_52 = Resistor [tolerance=±5% power=0.25W resistance=220 package=THT]
  100k_53 = Resistor [tolerance=±5% power=0.25W resistance=220 package=THT]
  100k44 = Resistor [tolerance=±5% power=0.25W resistance=220 package=THT]
  100k_54 = Resistor [tolerance=±5% power=0.25W resistance=220 package=THT]
  104_22 = Ceramic Capacitor [capacitance=100nF voltage=35V package="200 mil [THT, multilayer]"]
  104_23 = Ceramic Capacitor [capacitance=100nF voltage=35V package="200 mil [THT, multilayer]"]
  104_24 = Ceramic Capacitor [capacitance=100nF voltage=35V package="200 mil [THT, multilayer]"]
  104_25 = Ceramic Capacitor [capacitance=100nF voltage=35V package="200 mil [THT, multilayer]"]
  104_26 = Ceramic Capacitor [capacitance=100nF voltage=35V package="200 mil [THT, multilayer]"]
  104_27 = Ceramic Capacitor [capacitance=100nF voltage=35V package="200 mil [THT, multilayer]"]
  104_28 = Ceramic Capacitor [capacitance=100nF voltage=35V package="200 mil [THT, multilayer]"]
  R31 = Rotary Potentiometer (Small) [maximum_resistance=10kΩ knob_status=50% power=0.5W package=THT]
  R32 = Rotary Potentiometer (Small) [maximum_resistance=10kΩ knob_status=50% power=0.5W package=THT]
  R33 = Rotary Potentiometer (Small) [maximum_resistance=10kΩ knob_status=50% power=0.5W package=THT]
  R34 = Rotary Potentiometer (Small) [maximum_resistance=10kΩ knob_status=50% power=0.5W package=THT]
  R35 = Rotary Potentiometer (Small) [maximum_resistance=10kΩ knob_status=50% power=0.5W package=THT]
  R36 = Rotary Potentiometer (Small) [maximum_resistance=10kΩ knob_status=50% power=0.5W package=THT]
  R37 = Rotary Potentiometer (Small) [maximum_resistance=10kΩ knob_status=50% power=0.5W package=THT]
  R38 = Rotary Potentiometer (Small) [maximum_resistance=10kΩ knob_status=50% power=0.5W package=THT]
  SWITCH = IC, DIP package, 4 pins [chip_label=IC]
  104_29 = Ceramic Capacitor [capacitance=100nF voltage=35V package="200 mil [THT, multilayer]"]
  104_30 = Ceramic Capacitor [capacitance=100nF voltage=35V package="200 mil [THT, multilayer]"]
  SWITCH_2 = IC, DIP package, 4 pins [chip_label=IC]
  104_31 = Ceramic Capacitor [capacitance=100nF voltage=35V package="200 mil [THT, multilayer]"]
  104_32 = Ceramic Capacitor [capacitance=100nF voltage=35V package="200 mil [THT, multilayer]"]

nets:
  GND: R4.leg1, R5.leg1, R7.leg1, R8.leg1, R9.leg1, R10.leg1, R11.leg1, R12.leg1, R13.leg1, R16.leg1, R17.leg1, R18.leg1, R19.leg1, R20.leg1, R21.leg1, R22.leg1, TL082.pin4, 100k_5.Pin_0, 104.0, ʃ.Pin_1, 100k_9.Pin_0, 102.0, ʃ_3.Pin_1, 102_2.0, 100k_10.Pin_0, ▯.GND, TL082_2.pin4, ʃ_5.Pin_1, 102_3.1, 102_4.1, 100k_11.Pin_1, 102_5.1, 100k_12.Pin_1, ʃ_7.Pin_1, ʃ_8.Pin_1, 100k_13.Pin_1, 102_6.1, ʃ_11.Pin_1, 100k_14.Pin_1, 102_7.1, 100k_15.Pin_1, ʃ_12.Pin_1, ʃ_15.Pin_1, 100k_16.Pin_1, 102_8.1, 22k.Pin_1, 22k_2.Pin_1, -_9.E, 102_9.1, 22k_4.Pin_1, 102_10.1, LM358.pin4, 101.0, 1M_2.Pin_1, -_11.E, N.B, 10k_5.Pin_0, 104_3.0, L7809CV.GND, 220uF.-, 10uF.-, 104_4.0, 106.1, 475.1, 104_5.1, 104_6.1, 106_2.1, 106_3.1, 104_9.0, 1k_11.Pin_0, 1k_12.Pin_1, 105_9.0, CD4013.pin3, CD4013.pin5, CD4013.pin7, CD4013.pin9, CD4013.pin11, 220k1.Pin_1, 220k_2.Pin_0, -_14.E, -_15.E, TL082_3.pin4, LM358_2.pin4, LM358_3.pin4, LM358_4.pin4, TL082_4.pin4, -_17.Pin_0, -_18.Pin_0, 100k_20.Pin_1, 100k_21.Pin_1, 47k_3.Pin_0, 47k_4.Pin_1, -_21.Pin_1, -_22.Pin_1, 100k_33.Pin_1, 100k_34.Pin_1, 104_10.0, 104_11.0, 104_16.1, R23.leg1, R25.leg1, R26.leg1, R27.leg1, R28.leg1, R29.leg1, 106_4.1, 475_2.1, 104_17.1, 104_18.1, 106_5.1, 106_6.1, 104_21.0, 1k_15.Pin_0, 1k_16.Pin_1, 105_14.0, CD4013_2.pin3, CD4013_2.pin5, CD4013_2.pin7, CD4013_2.pin9, CD4013_2.pin11, 220k_9.Pin_1, 220k_10.Pin_0, -_26.E, -_27.E, TL082_5.pin4, LM358_5.pin4, LM358_6.pin4, LM358_7.pin4, TL082_6.pin4, -_29.Pin_0, -_30.Pin_0, 100k_39.Pin_1, 100k_40.Pin_1, 47k_5.Pin_0, 47k_6.Pin_1, -_33.Pin_1, -_34.Pin_1, 100k_53.Pin_1, 100k44.Pin_1, 104_22.0, 104_23.0, 104_28.1, R31.leg1, R33.leg1, R34.leg1, R35.leg1, R36.leg1, R37.leg1
  N1: R4.wiper, 100k5.Pin_0
  N2: R4.leg2, R5.leg2, R16.leg2, ʃ_2.Pin_0, ʃ_4.Pin_0, ▯.5V, ʃ_6.Pin_0, ʃ_9.Pin_0, ʃ_10.Pin_0, ʃ_13.Pin_0, ʃ_14.Pin_0
  N3: R5.wiper, 100k3.Pin_0
  N4: R7.wiper, -_4.Pin_1
  N5: R7.leg2, ▯.D13/SCK
  N6: R8.wiper, -_3.Pin_1
  N7: R8.leg2, ▯.D4
  N8: R9.wiper, -.Pin_1
  N9: R9.leg2, ▯.D2
  N10: R10.wiper, 100k_3.Pin_0
  N11: R10.leg2, 10k_26.Pin_1
  N12: R11.wiper, -_7.Pin_1
  N13: R11.leg2, ▯.D6
  N14: R12.wiper, 100k.Pin_0
  N15: R12.leg2, 10k_12.Pin_1
  N16: R13.wiper, 105_5.0
  N17: R13.leg2, 22k.Pin_0, 103.1
  N18: R16.wiper, 100k4.Pin_0
  N19: R17.wiper, 100k_4.Pin_1
  N20: R17.leg2, 10k_31.Pin_0
  N21: R18.wiper, 100k_2.Pin_1
  N22: R18.leg2, 10k_17.Pin_0
  N23: R19.wiper, -_8.Pin_1
  N24: R19.leg2, ▯.D7
  N25: R20.wiper, -_2.Pin_1
  N26: R20.leg2, ▯.D3
  N27: R21.wiper, -_5.Pin_1
  N28: R21.leg2, ▯.D5
  N29: R22.wiper, -_6.Pin_1
  N30: R22.leg2, ▯.D8
  N31: 100k.Pin_1, 100k_2.Pin_0, 105.0
  N32: 100k_3.Pin_1, 100k_4.Pin_0, 105_2.1
  N33: -.Pin_0, -_2.Pin_0, -_3.Pin_0, -_4.Pin_0, -_5.Pin_0, 1k_2.Pin_0, ʃ.Pin_0, ʃ_2.Pin_1, 100k_9.Pin_1, 102.1
  N34: -_6.Pin_0, -_7.Pin_0, -_8.Pin_0, 1k.Pin_1, ʃ_3.Pin_0, ʃ_4.Pin_1, 102_2.1, 100k_10.Pin_1
  N35: TL082.pin1, 100k_8.Pin_1, 1k_3.Pin_0
  N36: TL082.pin2, 100k_8.Pin_0, 105.1
  N37: TL082.pin3, TL082.pin5, 100k_5.Pin_1, 100k_6.Pin_1
  N38: TL082.pin6, 100k_7.Pin_1, 105_2.0
  N39: TL082.pin7, 100k_7.Pin_0, 1k_4.Pin_0
  N40: TL082.pin8, 100k_6.Pin_0, 104.1, ▯.VIN, TL082_2.pin8, ʃ_16.Pin_0, 22k_3.Pin_1, LM358.pin8, 4_7k.Pin_0, 47k_2.Pin_0, 104_3.1, L7809CV.OUT, 10uF.+, 104_4.1, 104_5.0, 104_6.0, 104_9.1, 105_9.1, CD4013.pin14, TL082_3.pin8, LM358_2.pin8, LM358_3.pin8, LM358_4.pin8, TL082_4.pin8, 1M_3.Pin_1, 1M_4.Pin_1, 22k_7.Pin_1, 22k_8.Pin_0, 100k_31.Pin_1, 100k_32.Pin_1, 104_10.1, R23.leg2, R27.leg2, R28.leg2, R29.leg2, 104_17.0, 104_18.0, 104_21.1, 105_14.1, CD4013_2.pin14, TL082_5.pin8, LM358_5.pin8, LM358_6.pin8, LM358_7.pin8, TL082_6.pin8, 1M_5.Pin_1, 1M_6.Pin_1, 22k_11.Pin_1, 22k_12.Pin_0, 100k_51.Pin_1, 100k_52.Pin_1, 104_22.1, R31.leg2, R35.leg2, R36.leg2, R37.leg2
  N41: 1k_3.Pin_1, 105_3.0
  N42: 1k_4.Pin_1, 105_4.0
  N43: 105_3.1, 10k_7.Pin_1
  N44: 105_4.1, 10k_6.Pin_1
  N45: ▯.D9, 2_2k.Pin_1
  N46: ▯.D11/MOSI, 1k_10.Pin_0, ʃ_15.Pin_0, ʃ_16.Pin_1, 100k_16.Pin_0, 102_8.0
  N47: ▯.D12/MISO, 102_3.0, 1k_9.Pin_0, 100k_15.Pin_0, ʃ_12.Pin_0, ʃ_14.Pin_1
  N48: ▯.A7, ʃ_5.Pin_0, ʃ_6.Pin_1, 1k_5.Pin_0, 102_4.0, 100k_11.Pin_0
  N49: ▯.A6, 1k_6.Pin_0, 102_5.0, 100k_12.Pin_0, ʃ_7.Pin_0, ʃ_13.Pin_1
  N50: ▯.A5, 100k1.Pin_0
  N51: ▯.A4, 100k2.Pin_0
  N52: ▯.A3, 100k3.Pin_1
  N53: ▯.A2, 100k4.Pin_1
  N54: ▯.A1, 100k5.Pin_1
  N55: TL082_2.pin1, 10k.Pin_0, 2_2k_2.Pin_1
  N56: TL082_2.pin2, 10k.Pin_1
  N57: TL082_2.pin3, 2_2k.Pin_0
  N58: TL082_2.pin5, 105_5.1
  N59: TL082_2.pin6, 101.1, 47k.Pin_1
  N60: TL082_2.pin7, 47k.Pin_0, 10k_6.Pin_0, 10k_7.Pin_0
  N61: ʃ_8.Pin_0, ʃ_9.Pin_1, 100k_13.Pin_0, 1k_7.Pin_0, 102_6.0, 100k2.Pin_1
  N62: 1k_8.Pin_1, ʃ_10.Pin_1, ʃ_11.Pin_0, 100k_14.Pin_0, 102_7.0, 100k1.Pin_1
  N63: 22k_2.Pin_0, 103.0, 103_2.1
  N64: 103_2.0, 22k_3.Pin_0, -_9.C
  N65: -_9.B, 1M.Pin_0, 102_12.1
  N66: 1M.Pin_1, 102_9.0, -_10.Pin_0
  N67: -_10.Pin_1, 22k_4.Pin_0, 102_10.0, 10k_2.Pin_1, 10k_3.Pin_1
  N68: LM358.pin5, 1M_2.Pin_0, 105_6.0
  N69: LM358.pin6, LM358.pin7, 10k_4.Pin_0
  N70: 105_6.1, 4_7k.Pin_1, 2_2M.Pin_1, 102_11.1, -_11.C
  N71: 2_2M.Pin_0, 102_11.0, -_11.B, 104_2.1
  N72: 104_2.0, N.C, 220k.Pin_0
  N73: 220k.Pin_1, 47k_2.Pin_1
  N74: 10k_4.Pin_1, 102_12.0, 10k_5.Pin_1
  N75: L7809CV.IN, D1.cathode, 220uF.+
  N76: 106.0, -_13.C, LM358_4.pin3, LM358_4.pin6, -_19.Pin_1
  N77: 475.0, -_12.C, LM358_3.pin2, LM358_3.pin5, -_16.Pin_1
  N78: 106_2.0, 1k_14.Pin_0, 10k_19.Pin_0
  N79: 106_3.0, 1k_13.Pin_0, 10k_21.Pin_1
  N80: 104_7.0, LM358_2.pin3, 100k_20.Pin_0
  N81: 104_7.1, R25.wiper
  N82: 104_8.0, LM358_2.pin5, 100k_21.Pin_0
  N83: 104_8.1, R26.wiper
  N84: 105_7.0, R25.leg2
  N85: 105_8.1, R26.leg2
  N86: 1k_11.Pin_1, 10k_9.Pin_1, LM358_2.pin6
  N87: 1k_12.Pin_0, 10k_8.Pin_0, LM358_2.pin2
  N88: 10k_8.Pin_1, LM358_2.pin1, 100k_19.Pin_0
  N89: 10k_9.Pin_0, LM358_2.pin7, 100k_22.Pin_1
  N90: CD4013.pin2, -_19.Pin_0
  N91: CD4013.pin4, 103_4.1, LM358_4.pin7, 220k_5.Pin_1
  N92: CD4013.pin6, 220k_2.Pin_1, 103_5.1
  N93: CD4013.pin8, 220k1.Pin_0, 103_6.0
  N94: CD4013.pin10, 103_3.1, LM358_3.pin1, 220k_6.Pin_1
  N95: CD4013.pin12, -_16.Pin_0
  N96: 103_3.0, -_18.Pin_1, -_20.Pin_0
  N97: 103_4.0, -_17.Pin_1, -_23.Pin_0
  N98: 103_5.0, -_15.C, 22k_7.Pin_0
  N99: 105_10.0, 100k_19.Pin_1
  N100: 105_10.1, TL082_4.pin2, 100k_18.Pin_1, 100k_29.Pin_1, 100k19.Pin_1, 100k_35.Pin_1, 104_15.1
  N101: 105_11.0, 100k_22.Pin_0
  N102: 105_11.1, TL082_4.pin6, 100k_17.Pin_0, 100k_23.Pin_0, 100k_26.Pin_1, 100k_27.Pin_1, 104_13.1
  N103: 103_6.1, -_14.C, 22k_8.Pin_1
  N104: -_12.E, 47k_3.Pin_1
  N105: -_12.B, 220k_7.Pin_0, 1M_3.Pin_0
  N106: -_13.E, 47k_4.Pin_0
  N107: -_13.B, 220k_8.Pin_0, 1M_4.Pin_0
  N108: -_14.B, 10k_10.Pin_0
  N109: -_15.B, 10k_11.Pin_1
  N110: TL082_3.pin1, TL082_3.pin2, 10k_12.Pin_0, 10k_13.Pin_0, 10k_14.Pin_0
  N111: TL082_3.pin3, 100k_28.Pin_0
  N112: TL082_3.pin5, 100k_24.Pin_1
  N113: TL082_3.pin6, TL082_3.pin7, 10k_15.Pin_1, 10k_16.Pin_1, 10k_17.Pin_1
  N114: LM358_3.pin3, 220k_3.Pin_0, 220k_6.Pin_0
  N115: LM358_3.pin6, LM358_3.pin7, 22k_6.Pin_0
  N116: LM358_4.pin1, LM358_4.pin2, 22k_5.Pin_0
  N117: LM358_4.pin5, 220k_4.Pin_0, 220k_5.Pin_0
  N118: TL082_4.pin1, 100k_28.Pin_1, 100k_30.Pin_0, 104_14.0, R30.wiper
  N119: TL082_4.pin3, TL082_4.pin5, 100k_31.Pin_0, 100k_34.Pin_0
  N120: TL082_4.pin7, 100k_24.Pin_0, 100k_25.Pin_0, 104_12.0, R24.leg1
  N121: -_20.Pin_1, 100k_17.Pin_1
  N122: 100k_18.Pin_0, SWITCH_2.pin3, 104_32.0
  N123: 100k_23.Pin_1, SWITCH_2.pin1, 104_31.0
  N124: 220k_3.Pin_1, 220k_4.Pin_1, 100k_32.Pin_0, 100k_33.Pin_0
  N125: 220k_7.Pin_1, R27.wiper
  N126: 220k_8.Pin_1, R28.wiper
  N127: 100k_25.Pin_1, 100k_26.Pin_0, 104_11.1
  N128: 100k_27.Pin_0, R24.wiper
  N129: 10k_18.Pin_0, R23.wiper
  N130: 10k_18.Pin_1, 10k_19.Pin_1, -_21.Pin_0, 104_12.1, 104_13.0
  N131: 10k_20.Pin_0, 10k_21.Pin_0, -_22.Pin_0, 104_14.1, 104_15.0
  N132: 10k_20.Pin_1, R29.wiper
  N133: 100k_29.Pin_0, R30.leg1
  N134: 100k19.Pin_0, 100k_30.Pin_1, 104_16.0
  N135: -_23.Pin_1, 100k_35.Pin_0
  N136: 106_4.0, -_25.C, LM358_7.pin3, LM358_7.pin6, -_31.Pin_1
  N137: 475_2.0, -_24.C, LM358_6.pin2, LM358_6.pin5, -_28.Pin_1
  N138: 106_5.0, 1k_18.Pin_0, 10k_33.Pin_0
  N139: 106_6.0, 1k_17.Pin_0, 10k_35.Pin_1
  N140: 104_19.0, LM358_5.pin3, 100k_39.Pin_0
  N141: 104_19.1, R33.wiper
  N142: 104_20.0, LM358_5.pin5, 100k_40.Pin_0
  N143: 104_20.1, R34.wiper
  N144: 105_12.0, R33.leg2
  N145: 105_13.1, R34.leg2
  N146: 1k_15.Pin_1, 10k_23.Pin_1, LM358_5.pin6
  N147: 1k_16.Pin_0, 10k_22.Pin_0, LM358_5.pin2
  N148: 10k_22.Pin_1, LM358_5.pin1, 100k_38.Pin_0
  N149: 10k_23.Pin_0, LM358_5.pin7, 100k_41.Pin_1
  N150: CD4013_2.pin2, -_31.Pin_0
  N151: CD4013_2.pin4, 103_8.1, LM358_7.pin7, 220k_13.Pin_1
  N152: CD4013_2.pin6, 220k_10.Pin_1, 103_9.1
  N153: CD4013_2.pin8, 220k_9.Pin_0, 103_10.0
  N154: CD4013_2.pin10, 103_7.1, LM358_6.pin1, 220k_14.Pin_1
  N155: CD4013_2.pin12, -_28.Pin_0
  N156: 103_7.0, -_30.Pin_1, -_32.Pin_0
  N157: 103_8.0, -_29.Pin_1, -_35.Pin_0
  N158: 103_9.0, -_27.C, 22k_11.Pin_0
  N159: 105_15.0, 100k_38.Pin_1
  N160: 105_15.1, TL082_6.pin2, 100k_37.Pin_1, 100k_48.Pin_1, 100k_49.Pin_1, 100k_54.Pin_1, 104_27.1
  N161: 105_16.0, 100k_41.Pin_0
  N162: 105_16.1, TL082_6.pin6, 100k_36.Pin_0, 100k_42.Pin_0, 100k_45.Pin_1, 100k_46.Pin_1, 104_25.1
  N163: 103_10.1, -_26.C, 22k_12.Pin_1
  N164: -_24.E, 47k_5.Pin_1
  N165: -_24.B, 220k_15.Pin_0, 1M_5.Pin_0
  N166: -_25.E, 47k_6.Pin_0
  N167: -_25.B, 220k_16.Pin_0, 1M_6.Pin_0
  N168: -_26.B, 10k_24.Pin_0
  N169: -_27.B, 10k_25.Pin_1
  N170: TL082_5.pin1, TL082_5.pin2, 10k_26.Pin_0, 10k_27.Pin_0, 10k_28.Pin_0
  N171: TL082_5.pin3, 100k_47.Pin_0
  N172: TL082_5.pin5, 100k_43.Pin_1
  N173: TL082_5.pin6, TL082_5.pin7, 10k_29.Pin_1, 10k_30.Pin_1, 10k_31.Pin_1
  N174: LM358_6.pin3, 220k_11.Pin_0, 220k_14.Pin_0
  N175: LM358_6.pin6, LM358_6.pin7, 22k_10.Pin_0
  N176: LM358_7.pin1, LM358_7.pin2, 22k_9.Pin_0
  N177: LM358_7.pin5, 220k_12.Pin_0, 220k_13.Pin_0
  N178: TL082_6.pin1, 100k_47.Pin_1, 100k_50.Pin_0, 104_26.0, R38.wiper
  N179: TL082_6.pin3, TL082_6.pin5, 100k_51.Pin_0, 100k44.Pin_0
  N180: TL082_6.pin7, 100k_43.Pin_0, 100k_44.Pin_0, 104_24.0, R32.leg1
  N181: -_32.Pin_1, 100k_36.Pin_1
  N182: 100k_37.Pin_0, SWITCH.pin2, 104_30.1
  N183: 100k_42.Pin_1, SWITCH.pin1, 104_29.1
  N184: 220k_11.Pin_1, 220k_12.Pin_1, 100k_52.Pin_0, 100k_53.Pin_0
  N185: 220k_15.Pin_1, R35.wiper
  N186: 220k_16.Pin_1, R36.wiper
  N187: 100k_44.Pin_1, 100k_45.Pin_0, 104_23.1
  N188: 100k_46.Pin_0, R32.wiper
  N189: 10k_32.Pin_0, R31.wiper
  N190: 10k_32.Pin_1, 10k_33.Pin_1, -_33.Pin_0, 104_24.1, 104_25.0
  N191: 10k_34.Pin_0, 10k_35.Pin_0, -_34.Pin_0, 104_26.1, 104_27.0
  N192: 10k_34.Pin_1, R37.wiper
  N193: 100k_48.Pin_0, R38.leg1
  N194: 100k_49.Pin_0, 100k_50.Pin_1, 104_28.0
  N195: -_35.Pin_1, 100k_54.Pin_0
  N196: SWITCH.pin3, 104_30.0
  N197: SWITCH.pin4, 104_29.0
  N198: SWITCH_2.pin2, 104_32.1
  N199: SWITCH_2.pin4, 104_31.1

notes:
  ▯
  D2 D3 D4 D5 D6 D7 D8 D9 D10 D11 D12
  D13
  5V A7 A6 A5 A4 A3 A2 A1 A0
  ⊕
  ⊖
  ⊕⊖
  NPNs (-) are 2n3904
  PNPs (+) are 2n3906
  diodes are 1n914
  shottky diodes are BAT46
  blank resistors are jumpers
  BC548
  Quad Creek
  Dylan Barry GPLv3 2025
  LOESS-LABS.NET
  all pots 100k linear
